# Fritzing sketch Espresso Controller (saved by Fritzing 0.9.3b)

parts:
  Part1 = Arduino Mega 2560 (Rev3)
  WeMos_D1_Mini_Relay_Shield_V1 = WeMos D1 Mini Relay Shield V2  # not connected
  WeMos_D1_Mini_Relay_Shield_V2 = WeMos D1 Mini Relay Shield V2  # not connected
  WeMos_D1_Mini_Relay_Shield_V3 = WeMos D1 Mini Relay Shield V2  # not connected
  WeMos_D1_Mini_Relay_Shield_V4 = WeMos D1 Mini Relay Shield V2  # not connected
  Arcade_Button_LED5 = Arcade Button with LED - Red
  Arcade_Button_LED6 = Arcade Button with LED - Red
  Arcade_Button_LED7 = Arcade Button with LED - Red
  Arcade_Button_LED8 = Arcade Button with LED - Red
  Arcade_Button_LED2 = Arcade Button with LED - Red
  Arcade_Button_LED3 = Arcade Button with LED - Red
  Arcade_Button_LED4 = Arcade Button with LED - Red
  Arcade_Button_LED1 = Arcade Button with LED - Red
  R2 = Resistor [tolerance=±5% resistance=68 package=THT]
  R3 = Resistor [tolerance=±5% resistance=68 package=THT]
  R4 = Resistor [tolerance=±5% resistance=68 package=THT]
  R5 = Resistor [tolerance=±5% resistance=68 package=THT]
  R6 = Resistor [tolerance=±5% resistance=68 package=THT]
  R7 = Resistor [tolerance=±5% resistance=68 package=THT]
  R8 = Resistor [tolerance=±5% resistance=68 package=THT]
  R9 = Resistor [tolerance=±5% resistance=68 package=THT]

nets:
  N1: Part1.3V3, Arcade_Button_LED5.terminal1, Arcade_Button_LED5.terminal5, Arcade_Button_LED6.terminal1, Arcade_Button_LED6.terminal5, Arcade_Button_LED7.terminal1, Arcade_Button_LED7.terminal5, Arcade_Button_LED8.terminal1, Arcade_Button_LED8.terminal5, Arcade_Button_LED2.terminal5, Arcade_Button_LED3.terminal5, Arcade_Button_LED4.terminal5, Arcade_Button_LED1.terminal5
  N2: Part1.D22, Arcade_Button_LED5.terminal2
  N3: Part1.D23, R4.Pin_1
  N4: Part1.D24, Arcade_Button_LED6.terminal2
  N5: Part1.D25, R3.Pin_1
  N6: Part1.D26, Arcade_Button_LED7.terminal2
  N7: Part1.D27, R2.Pin_1
  N8: Part1.D28, Arcade_Button_LED8.terminal2
  N9: Part1.D29, R9.Pin_1
  N10: Part1.D30, Arcade_Button_LED1.terminal2
  N11: Part1.D31, R5.Pin_1
  N12: Part1.D32, Arcade_Button_LED2.terminal2
  N13: Part1.D33, R6.Pin_1
  N14: Part1.D34, Arcade_Button_LED3.terminal2
  N15: Part1.D35, R7.Pin_1
  N16: Part1.D36, Arcade_Button_LED4.terminal2
  N17: Part1.D37, R8.Pin_1
  N18: Arcade_Button_LED5.terminal4, R4.Pin_0
  N19: Arcade_Button_LED6.terminal4, R3.Pin_0
  N20: Arcade_Button_LED7.terminal4, R2.Pin_0
  N21: Arcade_Button_LED8.terminal4, R9.Pin_0
  N22: Arcade_Button_LED2.terminal4, R6.Pin_0
  N23: Arcade_Button_LED3.terminal4, R7.Pin_0
  N24: Arcade_Button_LED4.terminal4, R8.Pin_0
  N25: Arcade_Button_LED1.terminal4, R5.Pin_0

notes:
  Coffee Machine Pins
  LEFT GH Buttons
  buttonPin_LST = 22; // the number of the pushbutton pin
  ledPin_LST = 23; // the number of the LED pin
  buttonPin_LGO = 24; // the number of the pushbutton pin
  ledPin_LGO = 25; // the number of the LED pin
  buttonPin_LSS = 26; // the number of the pushbutton pin
  ledPin_LSS = 27; // the number of the LED pin
  buttonPin_LDS = 28; // the number of the pushbutton pin
  ledPin_LDS = 29; // the number of the LED pin
  RIGHT GH Buttons
  buttonPin_RST = 30; // the number of the pushbutton pin
  ledPin_RST = 31; // the number of the LED pin
  buttonPin_RGO = 32; // the number of the pushbutton pin
  ledPin_RGO = 33; // the number of the LED pin
  buttonPin_RSS = 34; // the number of the pushbutton pin
  ledPin_RSS = 35; // the number of the LED pin
  buttonPin_RDS = 36; // the number of the pushbutton pin
  ledPin_RDS = 37; // the number of the LED pin
  RELAY PIN NUMBERS
  relayPin_LGH = 38;
  relayPin_RGH = 39;
  RelayPin_PUMP = 40;
  relayPin_TANK = 41;
  TANK SENSOR PIN
  tankSensorPin = 42;
  Flow Sensors
  flowSensorPin_LGH = 21; //INT[0] -Interrupt pin required for Flow sensor input
  flowSensorPin_RGH = 20; //INT[0] -Interrupt pin required for Flow sensor input

custom parts:
  Arcade Button with LED - Red: Arcade Button With LED
  Arcade Button with LED - Red: Arcade Button With LED
  Arcade Button with LED - Red: Arcade Button With LED
